// Logisim project datapath.circ as structural Verilog: 3 circuits, main circuit Datapath
module Datapath (
  input  Reset,
  input  Clear,
  input  Clear_2
);

  wire alu_1_zero, and_1_out, Clock_out, control_1_branch, control_1_escrevemem, control_1_escrevereg,
       control_1_lemem, control_1_memparareg, control_1_origalu, control_1_regdst, not_1_out;
  wire [1:0] control_1_opalu;
  wire [3:0] alucontrol_1_operation;
  wire [4:0] instructiondecode_1_rd, instructiondecode_1_rs, instructiondecode_1_rt, multiplexer_1_out;
  wire [5:0] instructiondecode_1_funct, instructiondecode_1_op;
  wire [7:0] wordaddress_1_wordaddress, wordaddress_2_wordaddress;
  wire [15:0] instructiondecode_1_immediate;
  wire [31:0] adder_1_out, alu_1_result, branchaddress_1_branchaddress, mips_ram_1_p7, mips_ram_2_p8,
       multiplexer_2_out, multiplexer_3_out, register_1_q, registerfile_1_p1, registerfile_1_p8,
       registerfile_1_p9, signextend_1_out_2;

  Register #(.width(32)) register_1 (
    .D(multiplexer_3_out), .Q(register_1_q), .clk(Clock_out), .clr(Reset));  // open: en
  Clock Clock (.out(Clock_out));
  WordAddress wordaddress_1 (.ByteAddress(register_1_q), .WordAddress(wordaddress_1_wordaddress));  // open: Unaligned
  InstructionDecode instructiondecode_1 (
    .Instruction(mips_ram_1_p7), .op(instructiondecode_1_op), .rs(instructiondecode_1_rs),
    .rt(instructiondecode_1_rt), .rd(instructiondecode_1_rd), .funct(instructiondecode_1_funct),
    .immediate(instructiondecode_1_immediate));  // open: shamt, address
  // MIPS_RAM mips_ram_1: pin names not known; wires that end beside it: wordaddress_1_wordaddress, 1'b0, 4'b1111, 1'b0, 1'b1, Clear, mips_ram_1_p7
  Control control_1 (
    .op(instructiondecode_1_op), .RegDst(control_1_regdst), .Branch(control_1_branch),
    .LeMem(control_1_lemem), .MemparaReg(control_1_memparareg), .OpALU(control_1_opalu),
    .EscreveMem(control_1_escrevemem), .OrigALU(control_1_origalu), .EscreveReg(control_1_escrevereg));
  Multiplexer #(.width(5), .enable("false")) multiplexer_1 (
    .in0(instructiondecode_1_rt), .in1(instructiondecode_1_rd), .out(multiplexer_1_out),
    .sel(control_1_regdst));
  Adder #(.width(32)) adder_1 (.a(32'h4), .b(register_1_q), .out(adder_1_out));  // open: cin, cout
  not not_1 (not_1_out, Clock_out);
  SignExtend signextend_1 (.in_1(instructiondecode_1_immediate), .out_2(signextend_1_out_2));
  // RegisterFile registerfile_1: pin names not known; wires that end beside it: registerfile_1_p1, not_1_out, control_1_escrevereg, multiplexer_1_out, instructiondecode_1_immediate, instructiondecode_1_rs, instructiondecode_1_rt, registerfile_1_p8, registerfile_1_p9
  Multiplexer #(.width(32), .enable("false")) multiplexer_2 (
    .in0(registerfile_1_p9), .in1(signextend_1_out_2), .out(multiplexer_2_out), .sel(control_1_origalu));
  WordAddress wordaddress_2 (.ByteAddress(alu_1_result), .WordAddress(wordaddress_2_wordaddress));  // open: Unaligned
  ALUcontrol alucontrol_1 (
    .funct(instructiondecode_1_funct), .OpALU(control_1_opalu), .Operation(alucontrol_1_operation));
  BranchAddress branchaddress_1 (
    .PC_4(adder_1_out), .Address(signextend_1_out_2), .BranchAddress(branchaddress_1_branchaddress));
  ALU alu_1 (
    .A(registerfile_1_p8), .B(multiplexer_2_out), .Operation(alucontrol_1_operation), .Zero(alu_1_zero),
    .Result(alu_1_result));  // open: Overflow
  // MIPS_RAM mips_ram_2: pin names not known; wires that end beside it: wordaddress_2_wordaddress, registerfile_1_p9, control_1_escrevemem, 4'b1111, Clock_out, control_1_lemem, Clear_2, mips_ram_2_p8
  Multiplexer #(.width(32), .enable("false")) multiplexer_3 (
    .in0(adder_1_out), .in1(branchaddress_1_branchaddress), .out(multiplexer_3_out), .sel(and_1_out));
  and and_1 (and_1_out, control_1_branch, alu_1_zero);
  Multiplexer #(.width(32), .enable("false")) multiplexer_4 (
    .in0(alu_1_result), .in1(mips_ram_2_p8), .out(registerfile_1_p1), .sel(control_1_memparareg));

  // Notes on the sheet:
  //   PC
  //   Opcode
  //   8c0a0000
  //   8c0b0004
  //   014b4820
  //   ac090008
  //   1000ffff
  //   Memória de Instruções
  //   Instruções
  //   Decodificador
  //   main:  lw $t2, 0($zero) 
  //   lw $t3, 4($zero)
  //   add $t1, $t2, $t3
  //   sw $t1, 8($zero)
  //   exit:  beq $zero, $zero, exit
  //   Controle
  //   Controle
  //   lw    001100011
  //   lw    001100011
  //   R     100010001
  //   sw    X00X00110
  //   beq   X10X01000
  //   Registradores
  //   Extensão
  //   Controle ALU
  //   0010 add
  //   0010 add
  //   0010 add
  //   0010 add
  //   0110 sub
  //   Controle ALU
  //   ALU
  //   Memória de Dados
  //   Branch
endmodule

module Control (
  input  [5:0] op,
  output RegDst,
  output Branch,
  output LeMem,
  output MemparaReg,
  output [1:0] OpALU,
  output EscreveMem,
  output OrigALU,
  output EscreveReg
);

  wire not_1_out, not_2_out, not_3_out, not_4_out, not_5_out, not_6_out, not_7_out, not_8_out, not_9_out,
       not_10_out, not_11_out, not_12_out, not_13_out, not_14_out, not_15_out, not_16_out, not_17_out,
       not_18_out, not_19_out, not_20_out, not_21_out, not_22_out, not_23_out, not_24_out, not_25_out,
       not_26_out, not_27_out, not_28_out;

  not not_1 (not_1_out, op[5]);
  not not_2 (not_2_out, op[0]);
  not not_3 (not_3_out, op[3]);
  not not_4 (not_4_out, op[4]);
  not not_5 (not_5_out, op[1]);
  not not_6 (not_6_out, op[2]);
  and R (OpALU[1], not_1_out, not_4_out, not_3_out, not_6_out, not_5_out, not_2_out);
  not not_7 (not_7_out, op[3]);
  not not_8 (not_8_out, op[2]);
  not not_9 (not_9_out, op[4]);
  and lw (LeMem, op[5], not_9_out, not_7_out, not_8_out, op[1], op[0]);
  not not_10 (not_10_out, op[2]);
  not not_11 (not_11_out, op[4]);
  and sw (EscreveMem, op[5], not_11_out, op[3], not_10_out, op[1], op[0]);
  not not_12 (not_12_out, op[3]);
  not not_13 (not_13_out, op[5]);
  not not_14 (not_14_out, op[1]);
  not not_15 (not_15_out, op[0]);
  not not_16 (not_16_out, op[4]);
  and beq (Branch, not_13_out, not_16_out, not_12_out, op[2], not_14_out, not_15_out);
  // NOT_Gate not_17 has open pins: in=open, out=not_17_out
  // NOT_Gate not_18 has open pins: in=open, out=not_18_out
  // NOT_Gate not_19 has open pins: in=open, out=not_19_out
  // NOT_Gate not_20 has open pins: in=open, out=not_20_out
  // NOT_Gate not_21 has open pins: in=open, out=not_21_out
  // NOT_Gate not_22 has open pins: in=open, out=not_22_out
  // AND_Gate jump has open pins: in0=not_20_out, in1=not_22_out, in2=not_19_out, in3=not_21_out, in4=not_17_out, in5=not_18_out, out=open
  or or_1 (OrigALU, LeMem, EscreveMem);
  or or_2 (EscreveReg, OpALU[1], LeMem);
  // NOT_Gate not_23 has open pins: in=open, out=not_23_out
  // NOT_Gate not_24 has open pins: in=open, out=not_24_out
  // NOT_Gate not_25 has open pins: in=open, out=not_25_out
  // NOT_Gate not_26 has open pins: in=open, out=not_26_out
  // NOT_Gate not_27 has open pins: in=open, out=not_27_out
  // NOT_Gate not_28 has open pins: in=open, out=not_28_out
  // AND_Gate addi has open pins: in0=not_24_out, in1=not_23_out, in2=not_25_out, in3=not_27_out, in4=not_26_out, in5=not_28_out, out=open

  assign MemparaReg = LeMem;
  assign OpALU[0] = Branch;
  assign RegDst = OpALU[1];
endmodule

module ALUcontrol (
  input  [1:0] OpALU,
  input  [5:0] funct,
  output [3:0] Operation
);

  wire and_1_out, not_1_out, not_2_out, not_3_out, or_1_out;

  or or_1 (or_1_out, funct[3], funct[0]);
  and and_1 (and_1_out, OpALU[1], funct[1]);
  and and_2 (Operation[0], OpALU[1], or_1_out);
  not not_1 (not_1_out, OpALU[1]);
  or or_2 (Operation[1], not_1_out, not_2_out);
  not not_2 (not_2_out, funct[2]);
  not not_3 (not_3_out, OpALU[0]);
  and and_3 (Operation[3], OpALU[0], not_3_out);
  or or_3 (Operation[2], OpALU[0], and_1_out);

  assign funct[4] = funct[5];
endmodule
